// Logisim project cpu_circuit.circ as structural Verilog: 2 circuits, main circuit main
module main (
  input  isInit
);

  wire and_1_out, clock_1_out, instruction_decoder_1_p2, instruction_decoder_1_p5, mask_checker_1_p1,
       mask_checker_1_p2, or_1_out, undriven, undriven_2, undriven_3;
  wire [3:0] instruction_decoder_1_p4, multiplexer_1_out;
  wire [15:0] instruction_ram_1_instruction, program_counter_1_instraddr;

  program_counter program_counter_1 (
    .CLK(clock_1_out), .WE(clock_1_out), .isJumping(or_1_out), .AddrImm({16{1'b0}}), .AddrReg({16{1'b0}}),
    .InitValue({16{1'b0}}), .JumpSrc(undriven), .isInit(isInit), .InstrAddr(program_counter_1_instraddr));
  or or_1 (or_1_out, and_1_out, undriven_2);
  and and_1 (and_1_out, mask_checker_1_p1, undriven_3);
  Clock clock_1 (.out(clock_1_out));
  instruction_RAM instruction_ram_1 (
    .InstrIN({16{1'b0}}), .InstrAddr(program_counter_1_instraddr), .WE(1'b0), .CLK(clock_1_out),
    .Instruction(instruction_ram_1_instruction));
  // mask_checker mask_checker_1: pin names not known; wires that end beside it: mask_checker_1_p1, mask_checker_1_p2
  // instruction_decoder instruction_decoder_1: pin names not known; wires that end beside it: instruction_ram_1_instruction, instruction_decoder_1_p2, mask_checker_1_p2, instruction_decoder_1_p4, instruction_decoder_1_p5
  Multiplexer #(.select(2), .width(4)) multiplexer_1 (
    .in0(4'b0000), .in1(instruction_decoder_1_p4), .in2(4'b0000), .out(multiplexer_1_out));  // open: in3, sel
  // control_unit control_unit_1: pin names not known
  // register_file register_file_1: pin names not known; wires that end beside it: multiplexer_1_out

  // Notes on the sheet:
  //   should WE = CLK for real?
  //   in this circuit there must not be input pins
  //   A Clock module should be better
  //   ra
  //   rd
  //   lui_rd
endmodule

module mask_checker (
  input  [2:0] mask,
  input  [2:0] flags,
  output equal
);

  Comparator #(.width(3)) comparator_1 (.a(mask), .b(flags), .eq(equal));  // open: gt, lt
endmodule
